// Logisim project structural_mux.circ as structural Verilog: 1 circuit, main circuit main
module main (
);

  wire multiplexer_1_out, multiplexer_2_out, multiplexer_3_out, multiplexer_4_out, multiplexer_5_out,
       multiplexer_6_out, multiplexer_7_out, multiplexer_8_out, multiplexer_9_out, undriven, undriven_2,
       undriven_3, undriven_4, undriven_5, undriven_6, undriven_7;

  Multiplexer #(.enable("false")) multiplexer_1 (
    .in0(undriven_2), .in1(undriven), .out(multiplexer_1_out), .sel(undriven_5));
  Multiplexer #(.enable("false")) multiplexer_2 (
    .in0(undriven_3), .in1(undriven_2), .out(multiplexer_2_out), .sel(undriven_5));
  Multiplexer #(.enable("false")) multiplexer_3 (
    .in0(undriven_4), .in1(undriven_3), .out(multiplexer_3_out), .sel(undriven_5));
  Multiplexer #(.enable("false")) multiplexer_4 (
    .in0(multiplexer_1_out), .in1(undriven), .out(multiplexer_4_out), .sel(undriven_6));
  Multiplexer #(.enable("false")) multiplexer_5 (
    .in0(multiplexer_2_out), .in1(multiplexer_1_out), .out(multiplexer_5_out), .sel(undriven_6));
  Multiplexer #(.enable("false")) multiplexer_6 (
    .in0(multiplexer_3_out), .in1(multiplexer_2_out), .out(multiplexer_6_out), .sel(undriven_6));
  Multiplexer #(.enable("false")) multiplexer_7 (
    .in0(multiplexer_4_out), .in1(undriven), .out(multiplexer_7_out), .sel(undriven_7));
  Multiplexer #(.enable("false")) multiplexer_8 (
    .in0(multiplexer_5_out), .in1(multiplexer_4_out), .out(multiplexer_8_out), .sel(undriven_7));
  Multiplexer #(.enable("false")) multiplexer_9 (
    .in0(multiplexer_6_out), .in1(multiplexer_5_out), .out(multiplexer_9_out), .sel(undriven_7));

  // Notes on the sheet:
  //   in_a[3]
  //   in_a[2]
  //   in_a[1]
  //   in_a[0]
  //   in_b[0]
  //   in_b[1]
  //   in_b[2]
  //   out[3]
  //   out[2]
  //   out[1]
  //   out[0]
endmodule
